# Fritzing sketch Verkabelung_Skizze (saved by Fritzing 0.9.3b)
breadboards: 1

parts:
  M1 = LILYGO TTGO-T SIM7000G
  A1 = Littlebee 40A ESC
  Bauteil1 = Lilypad Power Supply
  J1 = Basic Servo

nets:
  N1: M1.pin_2, M1.pin_18, A1.Pin_8
  N2: M1.pin_19, J1.pulse
  N3: A1.Pin_1, Bauteil1.GND
  N4: A1.Pin_2, Bauteil1.+
  N5: A1.Pin_6, J1.gnd
  N6: A1.Pin_7, J1.vcc

custom parts:
  LILYGO TTGO-T SIM7000G: LILYGO® TTGO T-SIM7000G Module ESP32-WROVER-B Chip WiFi Bluetooth 18560 Battery Holder Solar Charge Development Board.
  Littlebee 40A ESC: LittleBee 40A 2-4 LiPo Battery ESC Brushless Speed Controller for RC FPV Multicopter.
